// Logisim project somador.circ as structural Verilog
module meiasoma (
  input  a0,
  input  b0,
  output s0,
  output out_4
);

  and and_1 (out_4, a0, b0);
  xor xor_1 (s0, a0, b0);
endmodule

module somacompleta (
  input  in_1,
  input  in_2,
  input  in_3,
  output out_4,
  output out_5
);

  wire meiasoma_1_out_4, meiasoma_1_s0, meiasoma_2_out_4;

  meiasoma meiasoma_1 (.a0(in_2), .b0(in_3), .out_4(meiasoma_1_out_4), .s0(meiasoma_1_s0));
  meiasoma meiasoma_2 (.a0(in_1), .b0(meiasoma_1_s0), .out_4(meiasoma_2_out_4), .s0(out_4));
  or or_1 (out_5, meiasoma_1_out_4, meiasoma_2_out_4);
endmodule

module soma4bit (
  input  a0,
  input  b0,
  input  a1,
  input  b1,
  input  a2,
  input  b2,
  input  a3,
  input  b3,
  output s0,
  output s1,
  output s2,
  output s3
);

  wire _0_out_5, _1_out_5, _2_out_5;

  somacompleta _0 (.in_2(a0), .in_3(b0), .out_5(_0_out_5), .out_4(s0));  // open: in_1
  somacompleta _1 (.in_2(a1), .in_3(b1), .in_1(_0_out_5), .out_5(_1_out_5), .out_4(s1));
  somacompleta _2 (.in_2(a2), .in_3(b2), .in_1(_1_out_5), .out_5(_2_out_5), .out_4(s2));
  somacompleta _3 (.in_2(a3), .in_3(b3), .in_1(_2_out_5), .out_4(s3));  // open: out_5
endmodule
