// Logisim project testeaa.circ as structural Verilog
module meio_somador (
  input  A,
  input  B,
  output S,
  output Co
);

  xor xor_1 (S, A, B);
  and and_1 (Co, A, B);
endmodule

module somador_completo (
  input  Ci,
  input  A,
  input  B,
  output S,
  output Co
);

  wire meio_somador_1_co, meio_somador_1_s, meio_somador_2_co;

  meio_somador meio_somador_1 (.A(A), .B(B), .S(meio_somador_1_s), .Co(meio_somador_1_co));
  or or_1 (Co, meio_somador_1_co, meio_somador_2_co);
  meio_somador meio_somador_2 (.A(Ci), .B(meio_somador_1_s), .S(S), .Co(meio_somador_2_co));
endmodule

module somador_4bits (
  input  Ci,
  input  a0,
  input  a1,
  input  a2,
  input  a3,
  input  b0,
  input  b1,
  input  b2,
  input  b3,
  output s0,
  output s1,
  output s2,
  output s3,
  output Co,
  output Overflow
);

  wire somador_completo_1_co, somador_completo_2_co, somador_completo_3_co;

  somador_completo somador_completo_1 (.Ci(Ci), .A(a0), .B(b0), .S(s0), .Co(somador_completo_1_co));
  somador_completo somador_completo_2 (.Ci(somador_completo_1_co), .A(a1), .B(b1), .S(s1), .Co(somador_completo_2_co));
  somador_completo somador_completo_3 (.Ci(somador_completo_2_co), .A(a2), .B(b2), .S(s2), .Co(somador_completo_3_co));
  somador_completo somador_completo_4 (.Ci(somador_completo_3_co), .A(a3), .B(b3), .S(s3), .Co(Co));
  xor xor_1 (Overflow, somador_completo_3_co, s3);
endmodule

module calculadora (
  input  A0,
  input  Ci,
  input  A1,
  input  A2,
  input  A3,
  input  B0,
  input  B1,
  input  B2,
  input  B3,
  output S0,
  output S1,
  output S2,
  output S3,
  output Co,
  output Overflow
);

  wire bcd_to_7_decoder_1_a, bcd_to_7_decoder_1_b, bcd_to_7_decoder_1_c, bcd_to_7_decoder_1_d,
       bcd_to_7_decoder_1_e, bcd_to_7_decoder_1_f, bcd_to_7_decoder_1_g, bcd_to_7_decoder_2_a,
       bcd_to_7_decoder_2_b, bcd_to_7_decoder_2_c, bcd_to_7_decoder_2_d, bcd_to_7_decoder_2_e,
       bcd_to_7_decoder_2_f, bcd_to_7_decoder_2_g, bin_to_7_decoder_1_a, bin_to_7_decoder_1_b,
       bin_to_7_decoder_1_c, bin_to_7_decoder_1_d, bin_to_7_decoder_1_e, bin_to_7_decoder_1_f,
       bin_to_7_decoder_1_g;

  bcd_to_7_decoder bcd_to_7_decoder_1 (
    .Ai(A3), .Bi(A2), .Ci(A1), .Di(A0), .a(bcd_to_7_decoder_1_a), .b(bcd_to_7_decoder_1_b),
    .c(bcd_to_7_decoder_1_c), .d(bcd_to_7_decoder_1_d), .e(bcd_to_7_decoder_1_e), .f(bcd_to_7_decoder_1_f),
    .g(bcd_to_7_decoder_1_g));
  bcd_to_7_decoder bcd_to_7_decoder_2 (
    .Ai(B3), .Bi(B2), .Ci(B1), .Di(B0), .a(bcd_to_7_decoder_2_a), .b(bcd_to_7_decoder_2_b),
    .c(bcd_to_7_decoder_2_c), .d(bcd_to_7_decoder_2_d), .e(bcd_to_7_decoder_2_e), .f(bcd_to_7_decoder_2_f),
    .g(bcd_to_7_decoder_2_g));
  _7_Segment_Display u_7_segment_display_1 (
    .g(bcd_to_7_decoder_1_g), .f(bcd_to_7_decoder_1_f), .a(bcd_to_7_decoder_1_a), .b(bcd_to_7_decoder_1_b),
    .e(bcd_to_7_decoder_1_e), .d(bcd_to_7_decoder_1_d), .c(bcd_to_7_decoder_1_c));  // open: dp
  _7_Segment_Display u_7_segment_display_2 (
    .g(bcd_to_7_decoder_2_g), .f(bcd_to_7_decoder_2_f), .a(bcd_to_7_decoder_2_a), .b(bcd_to_7_decoder_2_b),
    .e(bcd_to_7_decoder_2_e), .d(bcd_to_7_decoder_2_d), .c(bcd_to_7_decoder_2_c));  // open: dp
  somador_4bits somador_4bits_1 (
    .Ci(Ci), .a0(A0), .a1(A1), .a2(A2), .a3(A3), .b0(B0), .b1(B1), .b2(B2), .b3(B3), .s0(S0), .s1(S1),
    .s2(S2), .s3(S3), .Co(Co), .Overflow(Overflow));
  bin_to_7_decoder bin_to_7_decoder_1 (
    .Ai(S3), .Bi(S2), .Ci(S1), .Di(S0), .a(bin_to_7_decoder_1_a), .b(bin_to_7_decoder_1_b),
    .c(bin_to_7_decoder_1_c), .d(bin_to_7_decoder_1_d), .e(bin_to_7_decoder_1_e), .f(bin_to_7_decoder_1_f),
    .g(bin_to_7_decoder_1_g));
  _7_Segment_Display u_7_segment_display_3 (
    .g(bin_to_7_decoder_1_g), .f(bin_to_7_decoder_1_f), .a(bin_to_7_decoder_1_a), .b(bin_to_7_decoder_1_b),
    .e(bin_to_7_decoder_1_e), .d(bin_to_7_decoder_1_d), .c(bin_to_7_decoder_1_c));  // open: dp
endmodule

module bcd_to_7_decoder (
  input  Ai,
  input  Bi,
  input  Ci,
  input  Di,
  output a,
  output b,
  output c,
  output d,
  output e,
  output f,
  output g
);

  wire and_1_out, and_2_out, and_3_out, and_4_out, and_5_out, and_6_out, and_7_out, and_8_out, and_9_out,
       and_10_out, and_11_out, and_12_out, and_13_out, and_14_out, and_15_out, and_16_out, and_17_out,
       and_18_out, not_1_out, not_2_out, not_3_out;

  not not_1 (not_1_out, Bi);
  not not_2 (not_2_out, Ci);
  not not_3 (not_3_out, Di);
  and and_1 (and_1_out, not_1_out, not_3_out);
  and and_2 (and_2_out, Bi, Di);
  and and_3 (and_3_out, not_1_out, Ci);
  and and_4 (and_4_out, not_2_out, not_3_out);
  and and_5 (and_5_out, Ci, Di);
  or or_1 (c, not_2_out, Di, Bi, Ai);
  and and_6 (and_6_out, not_1_out, not_3_out);
  and and_7 (and_7_out, not_1_out, Ci);
  and and_8 (and_8_out, Bi, not_2_out, Di);
  and and_9 (and_9_out, Ci, not_3_out);
  and and_10 (and_10_out, not_1_out, not_3_out);
  and and_11 (and_11_out, Ci, not_3_out);
  and and_12 (and_12_out, Ai, not_3_out);
  and and_13 (and_13_out, not_2_out, not_3_out);
  and and_14 (and_14_out, Bi, not_2_out);
  and and_15 (and_15_out, Bi, not_3_out);
  and and_16 (and_16_out, not_1_out, Ci);
  and and_17 (and_17_out, Bi, not_2_out);
  and and_18 (and_18_out, Ci, not_3_out);
  or or_2 (a, and_1_out, and_2_out, Ai, and_3_out);
  or or_3 (b, not_1_out, and_4_out, and_5_out, Ai);
  or or_4 (d, and_6_out, and_7_out, and_8_out, and_9_out, Ai);
  or or_5 (e, and_10_out, and_11_out, and_12_out);
  or or_6 (f, and_13_out, and_14_out, and_15_out, Ai);
  or or_7 (g, and_16_out, and_17_out, Ai, and_18_out);
endmodule

module bin_to_7_decoder (
  input  Ai,
  input  Bi,
  input  Ci,
  input  Di,
  output a,
  output b,
  output c,
  output d,
  output e,
  output f,
  output g
);

  wire and_1_out, and_2_out, and_3_out, and_4_out, and_5_out, and_6_out, and_7_out, and_8_out, and_9_out,
       and_10_out, and_11_out, and_12_out, and_13_out, and_14_out, and_15_out, and_16_out, and_17_out,
       and_18_out, and_19_out, and_20_out, and_21_out, and_22_out, and_23_out, and_24_out, and_25_out,
       and_26_out, and_27_out, and_28_out, and_29_out, and_30_out, and_31_out, and_32_out, not_1_out,
       not_2_out, not_3_out, not_4_out;

  not not_1 (not_1_out, Ai);
  not not_2 (not_2_out, Bi);
  not not_3 (not_3_out, Ci);
  not not_4 (not_4_out, Di);
  and and_1 (and_1_out, not_2_out, not_4_out);
  and and_2 (and_2_out, not_1_out, Ci);
  and and_3 (and_3_out, not_1_out, Bi, Di);
  and and_4 (and_4_out, Ai, not_2_out, not_3_out);
  and and_5 (and_5_out, Bi, Ci);
  and and_6 (and_6_out, not_1_out, not_3_out, not_4_out);
  and and_7 (and_7_out, not_2_out, not_3_out);
  and and_8 (and_8_out, not_1_out, Ci, Di);
  and and_9 (and_9_out, not_2_out, not_4_out);
  and and_10 (and_10_out, Ai, Bi, Ci);
  and and_11 (and_11_out, not_1_out, Bi);
  and and_12 (and_12_out, Ai, not_2_out);
  and and_13 (and_13_out, not_3_out, Di);
  and and_14 (and_14_out, not_2_out, not_3_out);
  and and_15 (and_15_out, not_2_out, Di);
  and and_16 (and_16_out, Bi, not_3_out, Di);
  and and_17 (and_17_out, not_1_out, not_2_out, not_4_out);
  and and_18 (and_18_out, not_2_out, Ci, Di);
  and and_19 (and_19_out, Ai, not_3_out);
  and and_20 (and_20_out, Bi, Ci, not_4_out);
  and and_21 (and_21_out, not_2_out, not_4_out);
  and and_22 (and_22_out, Ci, not_4_out);
  and and_23 (and_23_out, Ai, Ci);
  and and_24 (and_24_out, Ai, Bi);
  and and_25 (and_25_out, not_1_out, Bi, not_3_out);
  and and_26 (and_26_out, Ai, not_2_out);
  and and_27 (and_27_out, Ai, Ci);
  and and_28 (and_28_out, not_1_out, not_3_out, not_4_out);
  and and_29 (and_29_out, not_1_out, Bi, not_4_out);
  and and_30 (and_30_out, not_2_out, Ci);
  and and_31 (and_31_out, Bi, not_3_out);
  and and_32 (and_32_out, Ci, not_4_out);
  or or_1 (a, and_1_out, and_2_out, and_3_out, and_4_out, and_5_out);
  or or_2 (b, and_6_out, and_7_out, and_8_out, and_9_out, and_10_out);
  or or_3 (c, and_11_out, and_12_out, and_13_out, and_14_out, and_15_out);
  or or_4 (d, and_16_out, and_17_out, and_18_out, and_19_out, and_20_out);
  or or_5 (e, and_21_out, and_22_out, and_23_out, and_24_out);
  or or_6 (f, and_25_out, and_26_out, and_27_out, and_28_out, and_29_out);
  or or_7 (g, and_30_out, and_31_out, Ai, and_32_out);
endmodule

module ula_1bit (
  input  s1,
  input  a,
  input  s0,
  input  cin,
  input  binvert,
  input  b,
  output result,
  output cout
);

  wire and_1_out, mux_2_to_1_1_y, not_1_out, not_2_out, or_1_out, somador_completo_1_s;

  not not_1 (not_1_out, b);
  mux_2_to_1 mux_2_to_1_1 (.a(b), .s(binvert), .b(not_1_out), .y(mux_2_to_1_1_y));
  and and_1 (and_1_out, a, mux_2_to_1_1_y);
  or or_1 (or_1_out, a, mux_2_to_1_1_y);
  not not_2 (not_2_out, a);
  somador_completo somador_completo_1 (.Ci(cin), .A(a), .B(mux_2_to_1_1_y), .S(somador_completo_1_s), .Co(cout));
  mux_4_to_2 mux_4_to_2_1 (
    .s1(s1), .s0(s0), .a(and_1_out), .b(or_1_out), .c(not_2_out), .d(somador_completo_1_s), .o(result));
endmodule

module mux_2_to_1 (
  input  a,
  input  s,
  input  b,
  output y
);

  wire and_1_out, and_2_out, not_1_out;

  not not_1 (not_1_out, s);
  and and_1 (and_1_out, s, b);
  and and_2 (and_2_out, a, not_1_out);
  or or_1 (y, and_2_out, and_1_out);
endmodule

module mux_4_to_2 (
  input  s1,
  input  s0,
  input  a,
  input  b,
  input  c,
  input  d,
  output o
);

  wire and_1_out, and_2_out, and_3_out, and_4_out, not_1_out, not_2_out;

  not not_1 (not_1_out, s1);
  not not_2 (not_2_out, s0);
  and and_1 (and_1_out, not_2_out, not_1_out, a);
  and and_2 (and_2_out, s0, not_1_out, b);
  and and_3 (and_3_out, not_2_out, s1, c);
  and and_4 (and_4_out, s0, s1, d);
  or or_1 (o, and_1_out, and_2_out, and_3_out, and_4_out);
endmodule

module ula_4bits (
  input  b3,
  input  b2,
  input  b1,
  input  b0,
  input  a3,
  input  a2,
  input  a1,
  input  a0,
  input  Binvert,
  input  op1,
  input  op0,
  output s0,
  output s1,
  output s2,
  output s3,
  output cOut
);

  wire ula_1bit_1_cout, ula_1bit_2_cout, ula_1bit_3_cout;

  ula_1bit ula_1bit_1 (
    .s1(op1), .a(a0), .s0(op0), .cin(Binvert), .binvert(Binvert), .b(b0), .result(s0), .cout(ula_1bit_1_cout));
  ula_1bit ula_1bit_2 (
    .s1(op1), .a(a1), .s0(op0), .cin(ula_1bit_1_cout), .binvert(Binvert), .b(b1), .result(s1),
    .cout(ula_1bit_2_cout));
  ula_1bit ula_1bit_3 (
    .s1(op1), .a(a2), .s0(op0), .cin(ula_1bit_2_cout), .binvert(Binvert), .b(b2), .result(s2),
    .cout(ula_1bit_3_cout));
  ula_1bit ula_1bit_4 (
    .s1(op1), .a(a3), .s0(op0), .cin(ula_1bit_3_cout), .binvert(Binvert), .b(b3), .result(s3), .cout(cOut));
endmodule

module ula_74LS181 (
  input  [3:0] A,
  input  [3:0] B,
  input  [3:0] OP,
  output [3:0] S
);

  wire [3:0] and_1_out, and_2_out, and_3_out, nand_1_out, nor_1_out, nor_2_out, not_1_out, not_2_out,
       or_1_out, or_2_out, xnor_1_out, xor_1_out;

  assign and_1_out = ~A & B;  // AND_Gate and_1, 4 bits wide
  assign xor_1_out = A ^ B;  // XOR_Gate xor_1, 4 bits wide
  assign and_2_out = A & ~B;  // AND_Gate and_2, 4 bits wide
  assign and_3_out = A & B;  // AND_Gate and_3, 4 bits wide
  assign or_1_out = A | ~B;  // OR_Gate or_1, 4 bits wide
  assign or_2_out = A | B;  // OR_Gate or_2, 4 bits wide
  assign not_1_out = ~A;  // NOT_Gate not_1, 4 bits wide
  assign nor_1_out = ~(A | B);  // NOR_Gate nor_1, 4 bits wide
  assign nand_1_out = ~(A & B);  // NAND_Gate nand_1, 4 bits wide
  assign not_2_out = ~B;  // NOT_Gate not_2, 4 bits wide
  assign nor_2_out = ~(~A | B);  // NOR_Gate nor_2, 4 bits wide
  assign xnor_1_out = ~(A ^ B);  // XNOR_Gate xnor_1, 4 bits wide
  Multiplexer #(.select(4), .width(4)) multiplexer_1 (
    .in0(not_1_out), .in1(nor_1_out), .in2(and_1_out), .in3(4'b0000), .in4(nand_1_out), .in5(not_2_out),
    .in6(xor_1_out), .in7(and_2_out), .in8(nor_2_out), .in9(xnor_1_out), .in10(B), .in11(and_3_out),
    .in12(4'b1111), .in13(or_1_out), .in14(or_2_out), .in15(A), .out(S), .sel(OP));
endmodule
